// Logisim project комп_v5.circ as structural Verilog
module CPU (
  input  [31:0] Disk_in,
  input  Power,
  input  Clk,
  input  Reset,
  input  Start_CPU,
  input  [31:0] Execute_Device,
  input  [31:0] Data_in__U,
  input  [31:0] Data_in,
  output [23:0] Disk_Adress,
  output [31:0] Disk_out,
  output [2:0] CPU_condition
);

  wire A_to_Z, Access_to_RAM__US, ALU_ERROR, and_2_out, and_6_out, and_7_out, Clk_t, Comparation,
       initiate_load_device, \initiate_load_device_сomand , j_k_ff_1_q, j_k_ff_1_qn, L1, L2, L_complete,
       Load__loading_device, Load_A, Load_C, Load_PCP, Load_PCSP, Load_Program_select, Load_select__PC,
       Load_USP, Load_Y, loading_proqrams_device_1_load_ram, not_1_out, or_1_out, or_3_out, Pop, Push,
       register_1_q, Reset_RAM__CP, Reset_t, Stop_load_device, UP_DOWN__PC, UP_DOWN__US, UPop, UPush,
       Z_to_UCom_or_PCom, \пользовательская_остановка , \программная_остановка ;
  wire [2:0] ALU_select_B, C_select, Comand_Place, RAM_number_CPP__for_oper;
  wire [21:0] ALU_operation;
  wire [23:0] C1, L, loading_proqrams_device_1_adress_for_loading_to_comand_protocol, multiplexer_8_out,
       undriven_8;
  wire [31:0] A, ALU_result, bit_extender_2_out, C2, comand_protocol_programs_1_comand_64_95bit,
       comand_protocol_programs_1_comand_96_127bit, D, Data_in_Program_Comand, loading_proqrams_device_1__1,
       loading_proqrams_device_1__2, loading_proqrams_device_1__3, loading_proqrams_device_1__4,
       multiplexer_2_out, multiplexer_3_out, multiplexer_4_out, multiplexer_5_out, multiplexer_6_out,
       multiplexer_7_out, multiplexer_9_out, multiplexer_10_out, multiplexer_11_out, PC_out, undriven,
       undriven_2, undriven_3, undriven_4, undriven_5, undriven_6, undriven_7, undriven_9, undriven_10,
       undriven_11, undriven_12, undriven_13, UStack_out, Y, Z;
  wire [31:12] comand_protocol_programs_1_comand_32_63bit;

  or or_1 (or_1_out, 1'b0, Load__loading_device);
  Multiplexer #(.width(24), .disabled(0)) multiplexer_1 (
    .in0(L), .out(Disk_Adress), .sel(1'b0), .en(or_1_out));  // open: in1
  and and_1 (Clk_t, Power, Clk);
  D_Flip_Flop d_ff_1 (
    .clk(Start_CPU), .D(Power), .Q(CPU_condition[0]), .preset(1'b0), .en(Power), .reset(Reset_t));  // open: Qn
  or or_2 (Reset_t, ~Power, Reset);  // OR_Gate
  and and_2 (and_2_out, CPU_condition[0], Clk_t);
  J_K_Flip_Flop j_k_ff_1 (
    .J(Power), .clk(and_2_out), .K(Power), .Q(j_k_ff_1_q), .Qn(j_k_ff_1_qn), .preset(1'b0), .en(Power),
    .reset(Reset_t));
  and and_3 (CPU_condition[1], and_2_out, j_k_ff_1_q);
  and and_4 (CPU_condition[2], j_k_ff_1_qn, and_2_out);
  or or_3 (or_3_out, L2, loading_proqrams_device_1_load_ram);
  Multiplexer #(.width(32), .disabled(0), .enable("false")) multiplexer_2 (
    .in0(loading_proqrams_device_1__1), .in1(undriven), .out(multiplexer_2_out), .sel(L2));
  Loading_proqrams_device loading_proqrams_device_1 (
    .Data_in(Disk_in), .Clk(Clk_t), .Reset_Stop_loading(Stop_load_device), .Power(Power),
    .Load__Access_to_Load(initiate_load_device), ._1(loading_proqrams_device_1__1),
    ._2(loading_proqrams_device_1__2), ._3(loading_proqrams_device_1__3), ._4(loading_proqrams_device_1__4),
    .Loading_Complete(L_complete), .Load_RAM(loading_proqrams_device_1_load_ram),
    .Adress_for_loading_to_Comand_Protocol(loading_proqrams_device_1_adress_for_loading_to_comand_protocol),
    .Loading(Load__loading_device), .\Сдвиг_Адреса_загрузки__Диск (C1), .Adress_for_loading__for_Disk(L));
  Register #(.width(32)) u_A (.D(multiplexer_3_out), .en(Load_A), .Q(A), .clk(not_1_out), .clr(Reset_t));
  not not_1 (not_1_out, Clk_t);
  Multiplexer #(.width(32), .disabled(0)) multiplexer_3 (
    .in0(Data_in), .in1(Z), .out(multiplexer_3_out), .sel(A_to_Z), .en(Power));
  Comand_Protocol__Programs comand_protocol_programs_1 (
    .Power(Power), .\Сomand_Number (Z[23:0]),
    .comand_0_31bit({Load_USP, \программная_остановка , Load_C, \initiate_load_device_сomand , Z_to_UCom_or_PCom, Load_Y, Load_A, ALU_select_B, ALU_operation}),
    .comand_32_63bit({comand_protocol_programs_1_comand_32_63bit[31:16], Load_Program_select, comand_protocol_programs_1_comand_32_63bit[14], \программная_остановка , comand_protocol_programs_1_comand_32_63bit[12], UP_DOWN__US, UPop, Access_to_RAM__US, UPush, Reset_RAM__CP, Load_select__PC, UP_DOWN__PC, Load_PCSP, A_to_Z, Load_PCP, Pop, Push}),
    .comand_64_95bit(comand_protocol_programs_1_comand_64_95bit),
    .comand_96_127bit(comand_protocol_programs_1_comand_96_127bit), .Load_RAM(or_3_out),
    .Data_in_to_Ram_0_31(multiplexer_2_out), .Clk(Clk_t), .Data_in_to_Ram_32_63(multiplexer_4_out),
    .Comand_Place_ROM_or_Ram(Comand_Place), .Data_in_to_Ram_64_95(multiplexer_5_out),
    .Data_in_to_Ram_96_127(multiplexer_7_out), .\Сomand_Number_When_Loading_RAM (multiplexer_8_out),
    .Reset_RAM(Reset_RAM__CP), .RAM_Number__When_have_operation_with_RAM(RAM_number_CPP__for_oper),
    .Reset_all_RAM(Reset_t));
  Multiplexer #(.width(32), .disabled(0), .enable("false")) multiplexer_4 (
    .in0(loading_proqrams_device_1__2), .in1(undriven_2), .out(multiplexer_4_out), .sel(L2));
  Multiplexer #(.width(32), .disabled(0), .enable("false")) multiplexer_5 (
    .in0(loading_proqrams_device_1__3), .in1(undriven_3), .out(multiplexer_5_out), .sel(L2));
  Multiplexer #(.select(3), .width(32), .disabled(0)) multiplexer_6 (
    .in0(Execute_Device), .in1(Z), .in2(ALU_result), .in3(A), .in4(D), .in5(C2), .in6(undriven_6),
    .in7(undriven_7), .out(multiplexer_6_out), .en(Power));  // open: sel
  User_Stack user_stack_1 (
    .Z_Access_to_memory(Z), .Load_US_Pointer(undriven_5), .Data_in(Data_in), .Power(Power), .Clk(Clk_t),
    .Reset(Reset_t), .Load_US(Load_USP), .UP_0__DOWN_1(UP_DOWN__US), .Access(Access_to_RAM__US),
    .UPush(UPush), .UPop(UPop), .Data_out(UStack_out));
  Multiplexer #(.width(32), .disabled(0), .enable("false")) multiplexer_7 (
    .in0(loading_proqrams_device_1__4), .in1(undriven_4), .out(multiplexer_7_out), .sel(L2));
  Multiplexer #(.width(24), .disabled(0), .enable("false")) multiplexer_8 (
    .in0(loading_proqrams_device_1_adress_for_loading_to_comand_protocol), .in1(undriven_8),
    .out(multiplexer_8_out), .sel(L2));
  Register #(.width(32)) u_Y (.D(multiplexer_6_out), .en(Load_Y), .Q(Y), .clk(not_1_out), .clr(Reset_t));
  Multiplexer #(.width(32), .disabled(0)) multiplexer_9 (
    .in0(Data_in_Program_Comand), .in1(Data_in__U), .out(multiplexer_9_out), .sel(Z_to_UCom_or_PCom),
    .en(Power));
  Register #(.width(32)) IR_Z (.D(multiplexer_9_out), .en(CPU_condition[2]), .Q(Z), .clk(not_1_out), .clr(Reset_t));
  Register #(.width(32)) u_D (.D(Data_in), .en(CPU_condition[2]), .Q(D), .clk(not_1_out), .clr(Reset_t));
  Bit_Extender #(.in_width(32), .out_width(24)) bit_extender_1 (.in(C2), .out(C1));
  Register #(.width(32)) C (.D(multiplexer_10_out), .en(Load_C), .Q(C2), .clk(not_1_out), .clr(Reset_t));
  Multiplexer #(.select(3), .width(32), .disabled(0)) multiplexer_10 (
    .in0(A), .in1(Y), .in2(Z), .in3(D), .in4(ALU_result), .in5(undriven_9), .in6(undriven_10),
    .in7(undriven_11), .out(multiplexer_10_out), .sel(C_select), .en(Load_C));
  PC pc_1 (
    .sRam(Data_in), .Stack_Pointer__in(C2), .Z(Z), .Power(Power), .Reset(Reset_t), .Clk(Clk_t),
    .Load_PC_Pointer(Load_PCP), .Load_Stack_Pointer(Load_PCSP), .Push(Push), .Pop(Pop),
    .UP_0__DOWN_1(UP_DOWN__PC), .Load_Select(Load_select__PC), .Data_out(PC_out));
  assign bit_extender_2_out = {{24{1'b0}}, Z[31:24]};  // Bit_Extender bit_extender_2
  \ALU__СPU_GPU  \alu_сpu_gpu_1  (
    .Power(Power), .Operation(ALU_operation), .A(Y), .B(multiplexer_11_out), .C(ALU_result),
    .compare(Comparation), .Error(ALU_ERROR));
  Multiplexer #(.select(3), .width(32), .disabled(0)) multiplexer_11 (
    .in0(bit_extender_2_out), .in1(D), .in2(A), .in3(Y), .in4(Data_in), .in5(C2), .in6(undriven_12),
    .in7(undriven_13), .out(multiplexer_11_out), .sel(ALU_select_B), .en(Power));
  and and_5 (initiate_load_device, L1, \initiate_load_device_сomand );
  Pull_Resistor pull_resistor_1 (.node(\пользовательская_остановка ));
  Register #(.width(1)) register_1 (
    .D(initiate_load_device), .en(initiate_load_device), .Q(register_1_q), .clk(initiate_load_device),
    .clr(Stop_load_device));
  or or_4 (Stop_load_device, and_6_out, ~Power, L2, and_7_out, L_complete);  // OR_Gate
  Decoder #(.disabled(0)) decoder_1 (.out0(L1), .out1(L2), .sel(Load_Program_select), .en(Power));
  and and_6 (and_6_out, \пользовательская_остановка , register_1_q);
  buf and_7 (and_7_out, \программная_остановка );  // AND_Gate

  // Other names for the same wires on the sheet: Execute = CPU_condition[1]; Fetch = CPU_condition[2];
  //   Data_in__Users_Comand[31:0] = Data_in__U; ED[31:0] = Execute_Device

  // Notes on the sheet:
  //   условие выполнения
  //   условие выполнения
endmodule

module \ALU__СPU_GPU  (
  input  Power,
  input  [21:0] Operation,
  input  [31:0] A,
  input  [31:0] B,
  output [31:0] C,
  output Error,
  output compare
);

  wire and_2_out, and_3_out, and_4_out, bitselector_1_out, bitselector_2_out, bitselector_3_out,
       comparator_1_eq, comparator_1_gt, comparator_1_lt, comparator_2_p3, comparator_2_p4, comparator_2_p5,
       comparator_3_eq, comparator_4_eq, comparator_5_eq, comparator_6_eq, comparator_7_eq, comparator_8_eq,
       comparator_9_eq, comparator_10_eq, comparator_10_gt, comparator_10_lt, multiplexer_4_out, or_2_out;
  wire [0:0] pull_resistor_7_node;
  wire [4:0] priority_encoder_1_out, priority_encoder_2_out, priority_encoder_3_out, priority_encoder_4_out;
  wire [5:0] bitadder_1_out, bitadder_2_out, bitadder_4_out, bitadder_5_out;
  wire [6:0] bitadder_3_out, bitadder_6_out;
  wire [11:0] pull_resistor_9_node;
  wire [31:0] adder_1_p3, adder_2_out, adder_3_out, and_1_out, and_5_out, bit_extender_1_out,
       bit_extender_2_out, bit_extender_3_out, bit_extender_4_out, bit_extender_5_out, bit_extender_6_out,
       bit_extender_7_out, bit_extender_8_out, bit_extender_9_out, bit_extender_10_out, bit_extender_11_out,
       bit_extender_12_out, bit_extender_13_out, cos_1_p2, divider_1_p3, divider_2_out, divider_2_rem,
       divider_3_out, divider_3_rem, even_parity_1_out, even_parity_2_out, exponentiate_1_p3, fp_to_int_1_p2,
       fp_to_int_2_p4, fp_to_int_3_p2, increesor_1_out_2, increesor_2_out_2, increesor_3_out_2,
       increesor_4_out_2, int_to_fp_1_p2, ln_1_p2, log_1_p3, mod_1_p3, multiplexer_2_out, multiplier_1_p3,
       multiplier_2_cout, multiplier_2_out, multiplier_3_cout, multiplier_3_out, negator_1_out,
       negator_2_out, negator_3_out, odd_parity_1_out, odd_parity_2_out, or_1_out, or_4_out, pow_1_p2,
       pull_resistor_8_node, pull_resistor_10_node, pull_resistor_12_node, root_1_p3, shifter_1_out,
       shifter_2_out, shifter_3_out, shifter_4_out, shifter_5_out, shifter_6_out, shifter_7_out,
       shifter_8_out, shifter_9_out, shifter_10_out, shifter_11_out, shifter_12_out, shifter_13_out,
       shifter_14_out, shifter_15_out, sin_1_p2, sqrt_1_p2, subtractor_1_p3, subtractor_2_out,
       subtractor_3_out, tan_1_p2, xor_1_out, xor_2_out;

  Pull_Resistor pull_resistor_1 (.node(Operation));
  Pull_Resistor pull_resistor_2 (.node(B));
  Pull_Resistor pull_resistor_3 (.node(Power));
  Pull_Resistor pull_resistor_4 (.node(A));
  // Adder adder_1: pin names not known; wires that end beside it: A, B, adder_1_p3
  // Subtractor subtractor_1: pin names not known; wires that end beside it: A, B, subtractor_1_p3
  // Multiplier multiplier_1: pin names not known; wires that end beside it: A, B, multiplier_1_p3
  // Divider divider_1: pin names not known; wires that end beside it: A, B, divider_1_p3
  // Sin sin_1: pin names not known; wires that end beside it: A, sin_1_p2
  // Cos cos_1: pin names not known; wires that end beside it: A, cos_1_p2
  // Tan tan_1: pin names not known; wires that end beside it: A, tan_1_p2
  // Sqrt sqrt_1: pin names not known; wires that end beside it: A, sqrt_1_p2
  // Mod mod_1: pin names not known; wires that end beside it: A, B, mod_1_p3
  // Root root_1: pin names not known; wires that end beside it: A, B, root_1_p3
  // Log log_1: pin names not known; wires that end beside it: A, B, log_1_p3
  // Exponentiate exponentiate_1: pin names not known; wires that end beside it: A, B, exponentiate_1_p3
  // Pow pow_1: pin names not known; wires that end beside it: A, pow_1_p2
  // LN ln_1: pin names not known; wires that end beside it: A, ln_1_p2
  // Int_To_FP int_to_fp_1: pin names not known; wires that end beside it: A, int_to_fp_1_p2
  // FP_to_Int fp_to_int_1: pin names not known; wires that end beside it: A, fp_to_int_1_p2
  increesor increesor_1 (.in(A), .out_2(increesor_1_out_2));
  increesor increesor_2 (.in(B), .out_2(increesor_2_out_2));
  BitAdder #(.width(32)) bitadder_1 (.in0(A), .out(bitadder_1_out));
  assign bit_extender_1_out = {{26{1'b0}}, bitadder_1_out};  // Bit_Extender bit_extender_1
  BitAdder #(.width(32)) bitadder_2 (.in0(B), .out(bitadder_2_out));
  assign bit_extender_2_out = {{26{1'b0}}, bitadder_2_out};  // Bit_Extender bit_extender_2
  BitAdder #(.width(32)) bitadder_3 (.in0(A), .in1(B), .out(bitadder_3_out));
  assign bit_extender_3_out = {{25{1'b0}}, bitadder_3_out};  // Bit_Extender bit_extender_3
  assign or_1_out = A | B;  // OR_Gate or_1, 32 bits wide
  assign and_1_out = A & B;  // AND_Gate and_1, 32 bits wide
  assign xor_1_out = A ^ B;  // XOR_Gate xor_1, 32 bits wide
  assign odd_parity_1_out = A ^ B;  // Odd_Parity odd_parity_1, 32 bits wide
  assign even_parity_1_out = ~(A ^ B);  // Even_Parity even_parity_1, 32 bits wide
  BitSelector #(.width(32)) bitselector_1 (.in(A), .out(bitselector_1_out), .sel(Operation[21:17]));
  assign bit_extender_4_out = {{31{1'b0}}, bitselector_1_out};  // Bit_Extender bit_extender_4
  Comparator #(.width(32)) comparator_1 (
    .a(A), .b(B), .gt(comparator_1_gt), .eq(comparator_1_eq), .lt(comparator_1_lt));
  // Comparator comparator_2: pin names not known; wires that end beside it: A, B, comparator_2_p3, comparator_2_p4, comparator_2_p5
  Priority_Encoder #(.select(5), .disabled(0)) priority_encoder_1 (
    .in0(A[31]), .in1(A[30]), .in2(A[29]), .in3(A[28]), .in4(A[27]), .in5(A[26]), .in6(A[25]), .in7(A[24]),
    .in8(A[23]), .in9(A[22]), .in10(A[21]), .in11(A[20]), .in12(A[19]), .in13(A[18]), .in14(A[17]),
    .in15(A[16]), .in16(A[15]), .in17(A[14]), .in18(A[13]), .in19(A[12]), .in20(A[11]), .in21(A[10]),
    .in22(A[9]), .in23(A[8]), .in24(A[7]), .in25(A[6]), .in26(A[5]), .in27(A[4]), .in28(A[3]), .in29(A[2]),
    .in30(A[1]), .in31(A[0]), .out(priority_encoder_1_out));
  Priority_Encoder #(.select(5), .disabled(0)) priority_encoder_2 (
    .in0(B[31]), .in1(B[30]), .in2(B[29]), .in3(B[28]), .in4(B[27]), .in5(B[26]), .in6(B[25]), .in7(B[24]),
    .in8(B[23]), .in9(B[22]), .in10(B[21]), .in11(B[20]), .in12(B[19]), .in13(B[18]), .in14(B[17]),
    .in15(B[16]), .in16(B[15]), .in17(B[14]), .in18(B[13]), .in19(B[12]), .in20(B[11]), .in21(B[10]),
    .in22(B[9]), .in23(B[8]), .in24(B[7]), .in25(B[6]), .in26(B[5]), .in27(B[4]), .in28(B[3]), .in29(B[2]),
    .in30(B[1]), .in31(B[0]), .out(priority_encoder_2_out));
  assign bit_extender_5_out = {{27{1'b0}}, priority_encoder_1_out};  // Bit_Extender bit_extender_5
  assign bit_extender_6_out = {{27{1'b0}}, priority_encoder_2_out};  // Bit_Extender bit_extender_6
  Pull_Resistor pull_resistor_5 (.node(compare));
  Multiplexer #(.select(3), .disabled(0)) multiplexer_1 (
    .in0(1'b0), .in1(comparator_1_gt), .in2(comparator_1_eq), .in3(comparator_1_lt), .in4(1'b1),
    .in5(comparator_2_p3), .in6(comparator_2_p4), .in7(comparator_2_p5), .out(compare),
    .sel(Operation[12:10]), .en(Power));
  Multiplexer #(.select(5), .width(32)) multiplexer_2 (
    .in0(A), .in1(B), .in2(adder_1_p3), .in3(subtractor_1_p3), .in4(multiplier_1_p3), .in5(divider_1_p3),
    .in6(sin_1_p2), .in7(cos_1_p2), .in8(tan_1_p2), .in9(sqrt_1_p2), .in10(mod_1_p3), .in11(root_1_p3),
    .in12(log_1_p3), .in13(exponentiate_1_p3), .in14(pow_1_p2), .in15(ln_1_p2), .in16(int_to_fp_1_p2),
    .in17(fp_to_int_1_p2), .in18(bit_extender_1_out), .in19(bit_extender_2_out), .in20(bit_extender_3_out),
    .in21(or_1_out), .in22(and_1_out), .in23(xor_1_out), .in24(odd_parity_1_out), .in25(even_parity_1_out),
    .in26(increesor_1_out_2), .in27(increesor_2_out_2), .in28(bit_extender_5_out), .in29(bit_extender_6_out),
    .in30(bit_extender_4_out), .in31({32{1'b1}}), .out(multiplexer_2_out), .sel(Operation[4:0]), .en(Power));
  Negator #(.width(32)) negator_1 (.in(multiplexer_2_out), .out(negator_1_out));
  Shifter #(.width(32)) shifter_1 (.in(multiplexer_2_out), .\dist (Operation[9:5]), .out(shifter_1_out));
  Shifter #(.width(32), .shift("lr")) shifter_2 (.in(multiplexer_2_out), .\dist (Operation[9:5]), .out(shifter_2_out));
  Shifter #(.width(32), .shift("ar")) shifter_3 (.in(multiplexer_2_out), .\dist (Operation[9:5]), .out(shifter_3_out));
  Shifter #(.width(32), .shift("rl")) shifter_4 (.in(multiplexer_2_out), .\dist (Operation[9:5]), .out(shifter_4_out));
  Shifter #(.width(32), .shift("rr")) shifter_5 (.in(multiplexer_2_out), .\dist (Operation[9:5]), .out(shifter_5_out));
  Adder #(.width(32)) adder_2 (.a(A), .b(B), .out(adder_2_out));  // open: cin, cout
  Subtractor #(.width(32)) subtractor_2 (.a(A), .b(B), .out(subtractor_2_out));  // open: bin, bout
  Multiplier #(.width(32)) multiplier_2 (.a(A), .b(B), .out(multiplier_2_out), .cout(multiplier_2_cout));  // open: cin
  Divider #(.width(32)) divider_2 (.a(A), .b(B), .out(divider_2_out), .rem(divider_2_rem));  // open: upper
  Comparator #(.width(4)) comparator_3 (.a(Operation[16:13]), .b(4'b1011), .eq(comparator_3_eq));  // open: gt, lt
  Comparator #(.width(4)) comparator_4 (.a(Operation[16:13]), .b(4'b1100), .eq(comparator_4_eq));  // open: gt, lt
  Comparator #(.width(32)) comparator_5 (.a(B), .b({32{1'b0}}), .eq(comparator_5_eq));  // open: gt, lt
  // FP_to_Int fp_to_int_2: pin names not known; wires that end beside it: 4'b1011, 4'b1100, sin_1_p2, fp_to_int_2_p4
  // FP_to_Int fp_to_int_3: pin names not known; wires that end beside it: B, fp_to_int_3_p2
  or or_2 (or_2_out, comparator_3_eq, comparator_4_eq);
  Comparator #(.width(32)) comparator_6 (.a({32{1'b0}}), .b(fp_to_int_2_p4), .eq(comparator_6_eq));  // open: gt, lt
  Comparator #(.width(32)) comparator_7 (.a({32{1'b0}}), .b(fp_to_int_3_p2), .eq(comparator_7_eq));  // open: gt, lt
  Comparator #(.width(5)) comparator_8 (.a(Operation[4:0]), .b(5'b00101), .eq(comparator_8_eq));  // open: gt, lt
  Comparator #(.width(5)) comparator_9 (.a(Operation[4:0]), .b(5'b01000), .eq(comparator_9_eq));  // open: gt, lt
  and and_2 (and_2_out, or_2_out, comparator_5_eq);
  and and_3 (and_3_out, comparator_7_eq, comparator_8_eq);
  or or_3 (Error, and_2_out, and_3_out, and_4_out);
  and and_4 (and_4_out, comparator_6_eq, comparator_9_eq);
  Multiplexer #(.select(4), .width(32), .disabled(0)) multiplexer_3 (
    .in0(multiplexer_2_out), .in1(negator_1_out), .in2(shifter_1_out), .in3(shifter_2_out),
    .in4(shifter_3_out), .in5(shifter_4_out), .in6(shifter_5_out), .in7(adder_2_out), .in8(subtractor_2_out),
    .in9(multiplier_2_out), .in10(multiplier_2_cout), .in11(divider_2_out), .in12(divider_2_rem),
    .in13({32{1'b0}}), .in14({32{1'b0}}), .in15({32{1'b0}}), .out(C), .sel(Operation[16:13]), .en(Power));
  Pull_Resistor pull_resistor_6 (.node(C));
  Pull_Resistor pull_resistor_7 (.node(pull_resistor_7_node[0]));
  Pull_Resistor pull_resistor_8 (.node(pull_resistor_8_node));
  Pull_Resistor pull_resistor_9 (.node(pull_resistor_9_node));
  Pull_Resistor pull_resistor_10 (.node(pull_resistor_10_node));
  assign or_4_out = pull_resistor_8_node | pull_resistor_10_node;  // OR_Gate or_4, 32 bits wide
  assign and_5_out = pull_resistor_8_node & pull_resistor_10_node;  // AND_Gate and_5, 32 bits wide
  assign odd_parity_2_out = pull_resistor_8_node ^ pull_resistor_10_node;  // Odd_Parity odd_parity_2, 32 bits wide
  assign even_parity_2_out = ~(pull_resistor_8_node ^ pull_resistor_10_node);  // Even_Parity even_parity_2, 32 bits wide
  increesor increesor_3 (.in(pull_resistor_8_node), .out_2(increesor_3_out_2));
  increesor increesor_4 (.in(pull_resistor_10_node), .out_2(increesor_4_out_2));
  BitSelector #(.width(32)) bitselector_2 (
    .in(pull_resistor_8_node), .out(bitselector_2_out), .sel(pull_resistor_9_node[9:5]));
  BitSelector #(.width(32)) bitselector_3 (
    .in(pull_resistor_10_node), .out(bitselector_3_out), .sel(pull_resistor_9_node[9:5]));
  Adder #(.width(32)) adder_3 (
    .a(pull_resistor_8_node), .b(pull_resistor_10_node), .out(adder_3_out));  // open: cin, cout
  Subtractor #(.width(32)) subtractor_3 (
    .a(pull_resistor_8_node), .b(pull_resistor_10_node), .out(subtractor_3_out));  // open: bin, bout
  Multiplier #(.width(32)) multiplier_3 (
    .a(pull_resistor_8_node), .b(pull_resistor_10_node), .out(multiplier_3_out), .cout(multiplier_3_cout));  // open: cin
  Divider #(.width(32)) divider_3 (
    .a(pull_resistor_8_node), .b(pull_resistor_10_node), .out(divider_3_out), .rem(divider_3_rem));  // open: upper
  Negator #(.width(32)) negator_2 (.in(pull_resistor_8_node), .out(negator_2_out));
  Negator #(.width(32)) negator_3 (.in(pull_resistor_10_node), .out(negator_3_out));
  Shifter #(.width(32)) shifter_6 (.in(pull_resistor_8_node), .\dist (pull_resistor_9_node[9:5]), .out(shifter_6_out));
  Shifter #(.width(32), .shift("lr")) shifter_7 (
    .in(pull_resistor_8_node), .\dist (pull_resistor_9_node[9:5]), .out(shifter_7_out));
  Shifter #(.width(32), .shift("ar")) shifter_8 (
    .in(pull_resistor_8_node), .\dist (pull_resistor_9_node[9:5]), .out(shifter_8_out));
  Shifter #(.width(32), .shift("rl")) shifter_9 (
    .in(pull_resistor_8_node), .\dist (pull_resistor_9_node[9:5]), .out(shifter_9_out));
  Shifter #(.width(32), .shift("rr")) shifter_10 (
    .in(pull_resistor_8_node), .\dist (pull_resistor_9_node[9:5]), .out(shifter_10_out));
  Shifter #(.width(32)) shifter_11 (
    .in(pull_resistor_10_node), .\dist (pull_resistor_9_node[9:5]), .out(shifter_11_out));
  Shifter #(.width(32), .shift("lr")) shifter_12 (
    .in(pull_resistor_10_node), .\dist (pull_resistor_9_node[9:5]), .out(shifter_12_out));
  Shifter #(.width(32), .shift("ar")) shifter_13 (
    .in(pull_resistor_10_node), .\dist (pull_resistor_9_node[9:5]), .out(shifter_13_out));
  Shifter #(.width(32), .shift("rl")) shifter_14 (
    .in(pull_resistor_10_node), .\dist (pull_resistor_9_node[9:5]), .out(shifter_14_out));
  Shifter #(.width(32), .shift("rr")) shifter_15 (
    .in(pull_resistor_10_node), .\dist (pull_resistor_9_node[9:5]), .out(shifter_15_out));
  assign bit_extender_7_out = {{26{1'b0}}, bitadder_4_out};  // Bit_Extender bit_extender_7
  BitAdder #(.width(32)) bitadder_4 (.in0(pull_resistor_8_node), .out(bitadder_4_out));
  BitAdder #(.width(32)) bitadder_5 (.in0(pull_resistor_10_node), .out(bitadder_5_out));
  assign bit_extender_8_out = {{26{1'b0}}, bitadder_5_out};  // Bit_Extender bit_extender_8
  BitAdder #(.width(32)) bitadder_6 (.in0(pull_resistor_8_node), .in1(pull_resistor_10_node), .out(bitadder_6_out));
  assign bit_extender_9_out = {{25{1'b0}}, bitadder_6_out};  // Bit_Extender bit_extender_9
  assign xor_2_out = pull_resistor_8_node ^ pull_resistor_10_node;  // XOR_Gate xor_2, 32 bits wide
  assign bit_extender_10_out = {{31{1'b0}}, bitselector_2_out};  // Bit_Extender bit_extender_10
  assign bit_extender_11_out = {{31{1'b0}}, bitselector_3_out};  // Bit_Extender bit_extender_11
  Comparator #(.width(32)) comparator_10 (
    .a(pull_resistor_8_node), .b(pull_resistor_10_node), .gt(comparator_10_gt), .eq(comparator_10_eq),
    .lt(comparator_10_lt));
  Priority_Encoder #(.select(5), .disabled(0)) priority_encoder_3 (
    .in0(pull_resistor_8_node[31]), .in1(pull_resistor_8_node[30]), .in2(pull_resistor_8_node[29]),
    .in3(pull_resistor_8_node[28]), .in4(pull_resistor_8_node[27]), .in5(pull_resistor_8_node[26]),
    .in6(pull_resistor_8_node[25]), .in7(pull_resistor_8_node[24]), .in8(pull_resistor_8_node[23]),
    .in9(pull_resistor_8_node[22]), .in10(pull_resistor_8_node[21]), .in11(pull_resistor_8_node[20]),
    .in12(pull_resistor_8_node[19]), .in13(pull_resistor_8_node[18]), .in14(pull_resistor_8_node[17]),
    .in15(pull_resistor_8_node[16]), .in16(pull_resistor_8_node[15]), .in17(pull_resistor_8_node[14]),
    .in18(pull_resistor_8_node[13]), .in19(pull_resistor_8_node[12]), .in20(pull_resistor_8_node[11]),
    .in21(pull_resistor_8_node[10]), .in22(pull_resistor_8_node[9]), .in23(pull_resistor_8_node[8]),
    .in24(pull_resistor_8_node[7]), .in25(pull_resistor_8_node[6]), .in26(pull_resistor_8_node[5]),
    .in27(pull_resistor_8_node[4]), .in28(pull_resistor_8_node[3]), .in29(pull_resistor_8_node[2]),
    .in30(pull_resistor_8_node[1]), .in31(pull_resistor_8_node[0]), .out(priority_encoder_3_out));
  Priority_Encoder #(.select(5), .disabled(0)) priority_encoder_4 (
    .in0(pull_resistor_10_node[31]), .in1(pull_resistor_10_node[30]), .in2(pull_resistor_10_node[29]),
    .in3(pull_resistor_10_node[28]), .in4(pull_resistor_10_node[27]), .in5(pull_resistor_10_node[26]),
    .in6(pull_resistor_10_node[25]), .in7(pull_resistor_10_node[24]), .in8(pull_resistor_10_node[23]),
    .in9(pull_resistor_10_node[22]), .in10(pull_resistor_10_node[21]), .in11(pull_resistor_10_node[20]),
    .in12(pull_resistor_10_node[19]), .in13(pull_resistor_10_node[18]), .in14(pull_resistor_10_node[17]),
    .in15(pull_resistor_10_node[16]), .in16(pull_resistor_10_node[15]), .in17(pull_resistor_10_node[14]),
    .in18(pull_resistor_10_node[13]), .in19(pull_resistor_10_node[12]), .in20(pull_resistor_10_node[11]),
    .in21(pull_resistor_10_node[10]), .in22(pull_resistor_10_node[9]), .in23(pull_resistor_10_node[8]),
    .in24(pull_resistor_10_node[7]), .in25(pull_resistor_10_node[6]), .in26(pull_resistor_10_node[5]),
    .in27(pull_resistor_10_node[4]), .in28(pull_resistor_10_node[3]), .in29(pull_resistor_10_node[2]),
    .in30(pull_resistor_10_node[1]), .in31(pull_resistor_10_node[0]), .out(priority_encoder_4_out));
  Multiplexer #(.select(2), .disabled(0)) multiplexer_4 (
    .in0(1'b0), .in1(comparator_10_gt), .in2(comparator_10_eq), .in3(comparator_10_lt),
    .out(multiplexer_4_out), .sel(pull_resistor_9_node[11:10]), .en(pull_resistor_7_node[0]));
  Pull_Resistor pull_resistor_11 (.node(multiplexer_4_out));
  assign bit_extender_12_out = {{27{1'b0}}, priority_encoder_3_out};  // Bit_Extender bit_extender_12
  assign bit_extender_13_out = {{27{1'b0}}, priority_encoder_4_out};  // Bit_Extender bit_extender_13
  Pull_Resistor pull_resistor_12 (.node(pull_resistor_12_node));
  Multiplexer #(.select(5), .width(32)) multiplexer_5 (
    .in0(adder_3_out), .in1(subtractor_3_out), .in2(multiplier_3_out), .in3(divider_3_out),
    .in4(negator_2_out), .in5(negator_3_out), .in6(shifter_6_out), .in7(shifter_7_out), .in8(shifter_8_out),
    .in9(shifter_9_out), .in10(shifter_10_out), .in11(shifter_11_out), .in12(shifter_12_out),
    .in13(shifter_13_out), .in14(shifter_14_out), .in15(shifter_15_out), .in16(bit_extender_7_out),
    .in17(bit_extender_8_out), .in18(bit_extender_9_out), .in19(or_4_out), .in20(and_5_out),
    .in21(xor_2_out), .in22(odd_parity_2_out), .in23(even_parity_2_out), .in24(increesor_3_out_2),
    .in25(increesor_4_out_2), .in26(bit_extender_12_out), .in27(bit_extender_13_out),
    .in28(bit_extender_10_out), .in29(bit_extender_11_out), .in30(multiplier_3_cout), .in31(divider_3_rem),
    .out(pull_resistor_12_node), .sel(pull_resistor_9_node[4:0]), .en(pull_resistor_7_node[0]));

  // Notes on the sheet:
  //   +
  //   _
  //   *
  //   /
  //   sin
  //   cos
  //   tg
  //   ln
  //   sqrt
  //   mod
  //   root
  //   log
  //   exponent
  //   pow
  //   int()->float()
  //   float()->int()
endmodule

module User_Stack (
  input  [31:0] Z_Access_to_memory,
  input  [31:0] Load_US_Pointer,
  input  [31:0] Data_in,
  input  Power,
  input  Clk,
  input  Reset,
  input  Load_US,
  input  UP_0__DOWN_1,
  input  Access,
  input  UPush,
  input  UPop,
  output [31:0] Data_out
);

  wire and_1_out, controlled_buffer_1_out, controlled_buffer_2_out, not_1_out, not_2_out, not_3_out,
       or_1_out, or_2_out, or_3_out;
  wire [23:0] adder_1_out, bit_extender_1_out, bit_extender_2_out, controlled_buffer_3_out, US_Pointer_q;

  Pull_Resistor pull_resistor_1 (.node(Load_US_Pointer));
  Pull_Resistor pull_resistor_2 (.node(Power));
  Pull_Resistor pull_resistor_3 (.node(Data_in));
  Pull_Resistor pull_resistor_4 (.node(Z_Access_to_memory));
  Pull_Resistor pull_resistor_5 (.node(UPop));
  Pull_Resistor pull_resistor_6 (.node(Access));
  Pull_Resistor pull_resistor_7 (.node(Clk));
  Pull_Resistor pull_resistor_8 (.node(UPush));
  Pull_Resistor pull_resistor_9 (.node(Load_US));
  Pull_Resistor pull_resistor_10 (.node(Reset));
  Pull_Resistor pull_resistor_11 (.node(UP_0__DOWN_1));
  Bit_Extender #(.in_width(32), .out_width(24)) bit_extender_1 (.in(Z_Access_to_memory), .out(bit_extender_1_out));
  Bit_Extender #(.in_width(32), .out_width(24)) bit_extender_2 (.in(Load_US_Pointer), .out(bit_extender_2_out));
  not not_1 (not_1_out, Access);
  or or_1 (or_1_out, Load_US, UP_0__DOWN_1);
  and and_1 (and_1_out, ~Load_US, ~UP_0__DOWN_1);  // AND_Gate
  or or_2 (or_2_out, UPush, UPop);
  assign controlled_buffer_1_out = not_1_out ? or_1_out : 1'bz;  // Controlled_Buffer controlled_buffer_1
  assign controlled_buffer_2_out = not_1_out ? or_3_out : 1'bz;  // Controlled_Buffer controlled_buffer_2
  or or_3 (or_3_out, and_1_out, UP_0__DOWN_1);
  Counter #(.width(24), .max('hffffff)) US_Pointer (
    .load(controlled_buffer_1_out), .D(bit_extender_2_out), .count(controlled_buffer_2_out),
    .Q(US_Pointer_q), .clk(or_2_out), .clr(Reset));  // open: carry
  assign controlled_buffer_3_out = not_1_out ? US_Pointer_q : 24'bz;  // Controlled_Buffer controlled_buffer_3
  Adder #(.width(24)) adder_1 (.a(bit_extender_1_out), .b(US_Pointer_q), .out(adder_1_out));  // open: cin, cout
  not not_2 (not_2_out, not_1_out);
  assign controlled_buffer_3_out = not_2_out ? adder_1_out : 24'bz;  // Controlled_Buffer controlled_buffer_4
  not not_3 (not_3_out, UPush);
  Pull_Resistor pull_resistor_12 (.node(Data_out));
  RAM #(.addrWidth(24), .dataWidth(32), .bus("separate")) ram_1 (
    .addr(controlled_buffer_3_out), .din(Data_in), .data(Data_out), .str(UPush), .sel(Power), .clk(Clk),
    .ld(not_3_out), .clr(Reset));
endmodule

module Comand_Protocol__Programs (
  input  Reset_all_RAM,
  input  [2:0] RAM_Number__When_have_operation_with_RAM,
  input  Power,
  input  [23:0] \Сomand_Number ,
  input  Load_RAM,
  input  Clk,
  input  [2:0] Comand_Place_ROM_or_Ram,
  input  [31:0] Data_in_to_Ram_0_31,
  input  [31:0] Data_in_to_Ram_32_63,
  input  [31:0] Data_in_to_Ram_64_95,
  input  [31:0] Data_in_to_Ram_96_127,
  input  [23:0] \Сomand_Number_When_Loading_RAM ,
  input  Reset_RAM,
  output [31:0] comand_0_31bit,
  output [31:0] comand_32_63bit,
  output [31:0] comand_64_95bit,
  output [31:0] comand_96_127bit
);

  wire decoder_1_out1, decoder_1_out2, decoder_1_out3, decoder_1_out4, decoder_1_out5, decoder_1_out6,
       decoder_1_out7, decoder_2_out1, decoder_2_out2, decoder_2_out3, decoder_2_out4, decoder_2_out5,
       decoder_2_out6, decoder_2_out7, nor_1_out, not_1_out, not_2_out, not_3_out, not_4_out, not_5_out,
       not_6_out, not_7_out, not_8_out, not_9_out, not_10_out, not_11_out, not_12_out, not_13_out,
       not_14_out, not_15_out, not_16_out, not_17_out, not_18_out, not_19_out, not_20_out, not_21_out,
       not_22_out, not_23_out, not_24_out, not_25_out, not_26_out, not_27_out, not_28_out, or_1_out,
       or_2_out, or_3_out, or_4_out, or_5_out, or_6_out, or_7_out;
  wire [23:0] multiplexer_1_out, multiplexer_2_out, multiplexer_3_out, multiplexer_4_out, multiplexer_5_out,
       multiplexer_6_out, multiplexer_7_out;
  wire [31:0] ram_1_data, ram_2_data, ram_3_data, ram_4_data, ram_5_data, ram_6_data, ram_7_data, ram_8_data,
       ram_9_data, ram_10_data, ram_11_data, ram_12_data, ram_13_data, ram_14_data, ram_15_data, ram_16_data,
       ram_17_data, ram_18_data, ram_19_data, ram_20_data, ram_21_data, ram_22_data, ram_23_data,
       ram_24_data, ram_25_data, ram_26_data, ram_27_data, ram_28_data, rom_1_data, rom_2_data, rom_3_data,
       rom_4_data;

  Pull_Resistor pull_resistor_1 (.node(Power));
  Pull_Resistor pull_resistor_2 (.node(\Сomand_Number ));
  Pull_Resistor pull_resistor_3 (.node(Clk));
  Pull_Resistor pull_resistor_4 (.node(Data_in_to_Ram_32_63));
  Pull_Resistor pull_resistor_5 (.node(Load_RAM));
  Pull_Resistor pull_resistor_6 (.node(Reset_all_RAM));
  Pull_Resistor pull_resistor_7 (.node(Comand_Place_ROM_or_Ram));
  Pull_Resistor pull_resistor_8 (.node(Data_in_to_Ram_64_95));
  Pull_Resistor pull_resistor_9 (.node(Data_in_to_Ram_0_31));
  Pull_Resistor pull_resistor_10 (.node(RAM_Number__When_have_operation_with_RAM));
  nor nor_1 (nor_1_out, Power, Reset_all_RAM);
  Decoder #(.select(3), .disabled(0)) decoder_1 (
    .out1(decoder_1_out1), .out2(decoder_1_out2), .out3(decoder_1_out3), .out4(decoder_1_out4),
    .out5(decoder_1_out5), .out6(decoder_1_out6), .out7(decoder_1_out7),
    .sel(RAM_Number__When_have_operation_with_RAM), .en(Reset_RAM));  // open: out0
  Decoder #(.select(3), .disabled(0)) decoder_2 (
    .out1(decoder_2_out1), .out2(decoder_2_out2), .out3(decoder_2_out3), .out4(decoder_2_out4),
    .out5(decoder_2_out5), .out6(decoder_2_out6), .out7(decoder_2_out7),
    .sel(RAM_Number__When_have_operation_with_RAM), .en(Load_RAM));  // open: out0
  Pull_Resistor pull_resistor_11 (.node(\Сomand_Number_When_Loading_RAM ));
  Pull_Resistor pull_resistor_12 (.node(Reset_RAM));
  Pull_Resistor pull_resistor_13 (.node(Data_in_to_Ram_96_127));
  or or_1 (or_1_out, decoder_1_out1, nor_1_out);
  or or_2 (or_2_out, decoder_1_out2, nor_1_out);
  or or_3 (or_3_out, decoder_1_out5, nor_1_out);
  or or_4 (or_4_out, nor_1_out, decoder_1_out3);
  or or_5 (or_5_out, nor_1_out, decoder_1_out4);
  or or_6 (or_6_out, nor_1_out, decoder_1_out6);
  or or_7 (or_7_out, nor_1_out, decoder_1_out7);
  Multiplexer #(.width(24)) multiplexer_1 (
    .in0(\Сomand_Number ), .in1(\Сomand_Number_When_Loading_RAM ), .out(multiplexer_1_out), .sel(Load_RAM),
    .en(Power));
  Multiplexer #(.width(24)) multiplexer_2 (
    .in0(\Сomand_Number ), .in1(\Сomand_Number_When_Loading_RAM ), .out(multiplexer_2_out), .sel(Load_RAM),
    .en(Power));
  Multiplexer #(.width(24)) multiplexer_3 (
    .in0(\Сomand_Number ), .in1(\Сomand_Number_When_Loading_RAM ), .out(multiplexer_3_out), .sel(Load_RAM),
    .en(Power));
  Multiplexer #(.width(24)) multiplexer_4 (
    .in0(\Сomand_Number ), .in1(\Сomand_Number_When_Loading_RAM ), .out(multiplexer_4_out), .sel(Load_RAM),
    .en(Power));
  Multiplexer #(.width(24)) multiplexer_5 (
    .in0(\Сomand_Number ), .in1(\Сomand_Number_When_Loading_RAM ), .out(multiplexer_5_out), .sel(Load_RAM),
    .en(Power));
  Multiplexer #(.width(24)) multiplexer_6 (
    .in0(\Сomand_Number ), .in1(\Сomand_Number_When_Loading_RAM ), .out(multiplexer_6_out), .sel(Load_RAM),
    .en(Power));
  Multiplexer #(.width(24)) multiplexer_7 (
    .in0(\Сomand_Number ), .in1(\Сomand_Number_When_Loading_RAM ), .out(multiplexer_7_out), .sel(Load_RAM),
    .en(Power));
  not not_1 (not_1_out, decoder_2_out1);
  not not_2 (not_2_out, decoder_2_out1);
  not not_3 (not_3_out, decoder_2_out1);
  not not_4 (not_4_out, decoder_2_out1);
  not not_5 (not_5_out, decoder_2_out2);
  not not_6 (not_6_out, decoder_2_out2);
  not not_7 (not_7_out, decoder_2_out2);
  not not_8 (not_8_out, decoder_2_out2);
  not not_9 (not_9_out, decoder_2_out3);
  not not_10 (not_10_out, decoder_2_out3);
  not not_11 (not_11_out, decoder_2_out3);
  not not_12 (not_12_out, decoder_2_out3);
  not not_13 (not_13_out, decoder_2_out4);
  not not_14 (not_14_out, decoder_2_out4);
  not not_15 (not_15_out, decoder_2_out4);
  not not_16 (not_16_out, decoder_2_out4);
  not not_17 (not_17_out, decoder_2_out5);
  not not_18 (not_18_out, decoder_2_out5);
  not not_19 (not_19_out, decoder_2_out5);
  not not_20 (not_20_out, decoder_2_out5);
  not not_21 (not_21_out, decoder_2_out6);
  not not_22 (not_22_out, decoder_2_out6);
  not not_23 (not_23_out, decoder_2_out6);
  not not_24 (not_24_out, decoder_2_out6);
  not not_25 (not_25_out, decoder_2_out7);
  not not_26 (not_26_out, decoder_2_out7);
  not not_27 (not_27_out, decoder_2_out7);
  not not_28 (not_28_out, decoder_2_out7);
  ROM #(.addrWidth(24), .dataWidth(32)) rom_1 (.addr(\Сomand_Number ), .data(rom_1_data), .sel(Power));
  ROM #(.addrWidth(24), .dataWidth(32)) rom_2 (.addr(\Сomand_Number ), .data(rom_2_data), .sel(Power));
  ROM #(.addrWidth(24), .dataWidth(32)) rom_3 (.addr(\Сomand_Number ), .data(rom_3_data), .sel(Power));
  ROM #(.addrWidth(24), .dataWidth(32)) rom_4 (.addr(\Сomand_Number ), .data(rom_4_data), .sel(Power));
  RAM #(.addrWidth(24), .dataWidth(32), .bus("separate")) ram_1 (
    .addr(multiplexer_1_out), .din(Data_in_to_Ram_0_31), .data(ram_1_data), .str(decoder_2_out1),
    .sel(Power), .clk(Clk), .ld(not_1_out), .clr(or_1_out));
  RAM #(.addrWidth(24), .dataWidth(32), .bus("separate")) ram_2 (
    .addr(multiplexer_1_out), .din(Data_in_to_Ram_32_63), .data(ram_2_data), .str(decoder_2_out1),
    .sel(Power), .clk(Clk), .ld(not_2_out), .clr(or_1_out));
  RAM #(.addrWidth(24), .dataWidth(32), .bus("separate")) ram_3 (
    .addr(multiplexer_1_out), .din(Data_in_to_Ram_64_95), .data(ram_3_data), .str(decoder_2_out1),
    .sel(Power), .clk(Clk), .ld(not_3_out), .clr(or_1_out));
  RAM #(.addrWidth(24), .dataWidth(32), .bus("separate")) ram_4 (
    .addr(multiplexer_1_out), .din(Data_in_to_Ram_96_127), .data(ram_4_data), .str(decoder_2_out1),
    .sel(Power), .clk(Clk), .ld(not_4_out), .clr(or_1_out));
  RAM #(.addrWidth(24), .dataWidth(32), .bus("separate")) ram_5 (
    .addr(multiplexer_2_out), .din(Data_in_to_Ram_0_31), .data(ram_5_data), .str(decoder_2_out2),
    .sel(Power), .clk(Clk), .ld(not_5_out), .clr(or_2_out));
  RAM #(.addrWidth(24), .dataWidth(32), .bus("separate")) ram_6 (
    .addr(multiplexer_2_out), .din(Data_in_to_Ram_32_63), .data(ram_6_data), .str(decoder_2_out2),
    .sel(Power), .clk(Clk), .ld(not_6_out), .clr(or_2_out));
  RAM #(.addrWidth(24), .dataWidth(32), .bus("separate")) ram_7 (
    .addr(multiplexer_2_out), .din(Data_in_to_Ram_64_95), .data(ram_7_data), .str(decoder_2_out2),
    .sel(Power), .clk(Clk), .ld(not_7_out), .clr(or_2_out));
  RAM #(.addrWidth(24), .dataWidth(32), .bus("separate")) ram_8 (
    .addr(multiplexer_2_out), .din(Data_in_to_Ram_96_127), .data(ram_8_data), .str(decoder_2_out2),
    .sel(Power), .clk(Clk), .ld(not_8_out), .clr(or_2_out));
  RAM #(.addrWidth(24), .dataWidth(32), .bus("separate")) ram_9 (
    .addr(multiplexer_3_out), .din(Data_in_to_Ram_0_31), .data(ram_9_data), .str(decoder_2_out3),
    .sel(Power), .clk(Clk), .ld(not_9_out), .clr(or_4_out));
  RAM #(.addrWidth(24), .dataWidth(32), .bus("separate")) ram_10 (
    .addr(multiplexer_3_out), .din(Data_in_to_Ram_32_63), .data(ram_10_data), .str(decoder_2_out3),
    .sel(Power), .clk(Clk), .ld(not_10_out), .clr(or_4_out));
  RAM #(.addrWidth(24), .dataWidth(32), .bus("separate")) ram_11 (
    .addr(multiplexer_3_out), .din(Data_in_to_Ram_64_95), .data(ram_11_data), .str(decoder_2_out3),
    .sel(Power), .clk(Clk), .ld(not_11_out), .clr(or_4_out));
  RAM #(.addrWidth(24), .dataWidth(32), .bus("separate")) ram_12 (
    .addr(multiplexer_3_out), .din(Data_in_to_Ram_96_127), .data(ram_12_data), .str(decoder_2_out3),
    .sel(Power), .clk(Clk), .ld(not_12_out), .clr(or_4_out));
  RAM #(.addrWidth(24), .dataWidth(32), .bus("separate")) ram_13 (
    .addr(multiplexer_4_out), .din(Data_in_to_Ram_0_31), .data(ram_13_data), .str(decoder_2_out4),
    .sel(Power), .clk(Clk), .ld(not_13_out), .clr(or_5_out));
  RAM #(.addrWidth(24), .dataWidth(32), .bus("separate")) ram_14 (
    .addr(multiplexer_4_out), .din(Data_in_to_Ram_32_63), .data(ram_14_data), .str(decoder_2_out4),
    .sel(Power), .clk(Clk), .ld(not_14_out), .clr(or_5_out));
  RAM #(.addrWidth(24), .dataWidth(32), .bus("separate")) ram_15 (
    .addr(multiplexer_4_out), .din(Data_in_to_Ram_64_95), .data(ram_15_data), .str(decoder_2_out4),
    .sel(Power), .clk(Clk), .ld(not_15_out), .clr(or_5_out));
  RAM #(.addrWidth(24), .dataWidth(32), .bus("separate")) ram_16 (
    .addr(multiplexer_4_out), .din(Data_in_to_Ram_96_127), .data(ram_16_data), .str(decoder_2_out4),
    .sel(Power), .clk(Clk), .ld(not_16_out), .clr(or_5_out));
  RAM #(.addrWidth(24), .dataWidth(32), .bus("separate")) ram_17 (
    .addr(multiplexer_5_out), .din(Data_in_to_Ram_0_31), .data(ram_17_data), .str(decoder_2_out5),
    .sel(Power), .clk(Clk), .ld(not_17_out), .clr(or_3_out));
  RAM #(.addrWidth(24), .dataWidth(32), .bus("separate")) ram_18 (
    .addr(multiplexer_5_out), .din(Data_in_to_Ram_32_63), .data(ram_18_data), .str(decoder_2_out5),
    .sel(Power), .clk(Clk), .ld(not_18_out), .clr(or_3_out));
  RAM #(.addrWidth(24), .dataWidth(32), .bus("separate")) ram_19 (
    .addr(multiplexer_5_out), .din(Data_in_to_Ram_64_95), .data(ram_19_data), .str(decoder_2_out5),
    .sel(Power), .clk(Clk), .ld(not_19_out), .clr(or_3_out));
  RAM #(.addrWidth(24), .dataWidth(32), .bus("separate")) ram_20 (
    .addr(multiplexer_5_out), .din(Data_in_to_Ram_96_127), .data(ram_20_data), .str(decoder_2_out5),
    .sel(Power), .clk(Clk), .ld(not_20_out), .clr(or_3_out));
  RAM #(.addrWidth(24), .dataWidth(32), .bus("separate")) ram_21 (
    .addr(multiplexer_6_out), .din(Data_in_to_Ram_0_31), .data(ram_21_data), .str(decoder_2_out6),
    .sel(Power), .clk(Clk), .ld(not_21_out), .clr(or_6_out));
  RAM #(.addrWidth(24), .dataWidth(32), .bus("separate")) ram_22 (
    .addr(multiplexer_6_out), .din(Data_in_to_Ram_32_63), .data(ram_22_data), .str(decoder_2_out6),
    .sel(Power), .clk(Clk), .ld(not_22_out), .clr(or_6_out));
  RAM #(.addrWidth(24), .dataWidth(32), .bus("separate")) ram_23 (
    .addr(multiplexer_6_out), .din(Data_in_to_Ram_64_95), .data(ram_23_data), .str(decoder_2_out6),
    .sel(Power), .clk(Clk), .ld(not_23_out), .clr(or_6_out));
  RAM #(.addrWidth(24), .dataWidth(32), .bus("separate")) ram_24 (
    .addr(multiplexer_6_out), .din(Data_in_to_Ram_96_127), .data(ram_24_data), .str(decoder_2_out6),
    .sel(Power), .clk(Clk), .ld(not_24_out), .clr(or_6_out));
  RAM #(.addrWidth(24), .dataWidth(32), .bus("separate")) ram_25 (
    .addr(multiplexer_7_out), .din(Data_in_to_Ram_0_31), .data(ram_25_data), .str(decoder_2_out7),
    .sel(Power), .clk(Clk), .ld(not_25_out), .clr(or_7_out));
  RAM #(.addrWidth(24), .dataWidth(32), .bus("separate")) ram_26 (
    .addr(multiplexer_7_out), .din(Data_in_to_Ram_32_63), .data(ram_26_data), .str(decoder_2_out7),
    .sel(Power), .clk(Clk), .ld(not_26_out), .clr(or_7_out));
  RAM #(.addrWidth(24), .dataWidth(32), .bus("separate")) ram_27 (
    .addr(multiplexer_7_out), .din(Data_in_to_Ram_64_95), .data(ram_27_data), .str(decoder_2_out7),
    .sel(Power), .clk(Clk), .ld(not_27_out), .clr(or_7_out));
  RAM #(.addrWidth(24), .dataWidth(32), .bus("separate")) ram_28 (
    .addr(multiplexer_7_out), .din(Data_in_to_Ram_96_127), .data(ram_28_data), .str(decoder_2_out7),
    .sel(Power), .clk(Clk), .ld(not_28_out), .clr(or_7_out));
  Multiplexer #(.select(3), .width(32), .disabled(0)) multiplexer_8 (
    .in0(rom_1_data), .in1(ram_1_data), .in2(ram_5_data), .in3(ram_9_data), .in4(ram_13_data),
    .in5(ram_17_data), .in6(ram_21_data), .in7(ram_25_data), .out(comand_0_31bit),
    .sel(Comand_Place_ROM_or_Ram), .en(Power));
  Multiplexer #(.select(3), .width(32), .disabled(0)) multiplexer_9 (
    .in0(rom_2_data), .in1(ram_2_data), .in2(ram_6_data), .in3(ram_10_data), .in4(ram_14_data),
    .in5(ram_18_data), .in6(ram_22_data), .in7(ram_26_data), .out(comand_32_63bit),
    .sel(Comand_Place_ROM_or_Ram), .en(Power));
  Multiplexer #(.select(3), .width(32), .disabled(0)) multiplexer_10 (
    .in0(rom_3_data), .in1(ram_3_data), .in2(ram_7_data), .in3(ram_11_data), .in4(ram_15_data),
    .in5(ram_19_data), .in6(ram_23_data), .in7(ram_27_data), .out(comand_64_95bit),
    .sel(Comand_Place_ROM_or_Ram), .en(Power));
  Multiplexer #(.select(3), .width(32), .disabled(0)) multiplexer_11 (
    .in0(rom_4_data), .in1(ram_4_data), .in2(ram_8_data), .in3(ram_12_data), .in4(ram_16_data),
    .in5(ram_20_data), .in6(ram_24_data), .in7(ram_28_data), .out(comand_96_127bit),
    .sel(Comand_Place_ROM_or_Ram), .en(Power));
  Pull_Resistor pull_resistor_14 (.node(comand_0_31bit));
  Pull_Resistor pull_resistor_15 (.node(comand_32_63bit));
  Pull_Resistor pull_resistor_16 (.node(comand_64_95bit));
  Pull_Resistor pull_resistor_17 (.node(comand_96_127bit));

  // Notes on the sheet:
  //   comand_64_95bit: pull=up
  //   comand_96_127bit: pull=up
  //   comand_0_31bit: pull=up
  //   comand_32_63bit: pull=up
endmodule

module increesor (
  input  [31:0] in,
  output [31:0] out_2
);

  Pull_Resistor pull_resistor_1 (.node(in));
  Pull_Resistor pull_resistor_2 (.node(out_2));
  Adder #(.width(32)) adder_1 (.a(in), .b(32'h1), .out(out_2));  // open: cin, cout
endmodule

module PC (
  input  [31:0] sRam,
  input  [31:0] Stack_Pointer__in,
  input  [31:0] Z,
  input  Power,
  input  Reset,
  input  Clk,
  input  Load_PC_Pointer,
  input  Load_Stack_Pointer,
  input  Push,
  input  Pop,
  input  UP_0__DOWN_1,
  input  Load_Select,
  output [31:0] Data_out
);

  wire and_1_out, and_2_out, not_1_out, or_1_out, or_2_out, or_3_out, or_4_out, or_5_out;
  wire [23:0] bit_extender_1_out, Stack_Pointer_q;
  wire [31:0] multiplexer_1_out, ram_1_data;

  Pull_Resistor pull_resistor_1 (.node(Reset));
  Pull_Resistor pull_resistor_2 (.node(Z));
  Pull_Resistor pull_resistor_3 (.node(Power));
  Pull_Resistor pull_resistor_4 (.node(Stack_Pointer__in));
  Pull_Resistor pull_resistor_5 (.node(Load_Stack_Pointer));
  Pull_Resistor pull_resistor_6 (.node(Load_PC_Pointer));
  Pull_Resistor pull_resistor_7 (.node(Clk));
  Pull_Resistor pull_resistor_8 (.node(sRam));
  Pull_Resistor pull_resistor_9 (.node(Pop));
  Pull_Resistor pull_resistor_10 (.node(Load_Select));
  Pull_Resistor pull_resistor_11 (.node(UP_0__DOWN_1));
  Pull_Resistor pull_resistor_12 (.node(Push));
  Bit_Extender #(.in_width(32), .out_width(24)) bit_extender_1 (.in(Stack_Pointer__in), .out(bit_extender_1_out));
  Multiplexer #(.select(2), .width(32)) multiplexer_1 (
    .in0(sRam), .in1(Stack_Pointer__in), .in2(Z), .in3(ram_1_data), .out(multiplexer_1_out),
    .sel({Pop, Load_Select}), .en(Power));
  or or_1 (or_1_out, Push, Pop);
  or or_2 (or_2_out, UP_0__DOWN_1, Load_PC_Pointer);
  or or_3 (or_3_out, UP_0__DOWN_1, Load_Stack_Pointer);
  or or_4 (or_4_out, UP_0__DOWN_1, and_1_out);
  and and_1 (and_1_out, ~Load_Stack_Pointer, ~UP_0__DOWN_1);  // AND_Gate
  and and_2 (and_2_out, ~UP_0__DOWN_1, ~Load_PC_Pointer);  // AND_Gate
  or or_5 (or_5_out, and_2_out, UP_0__DOWN_1);
  Counter #(.width(32), .max('hffffffff)) PC_Pointer (
    .load(or_2_out), .D(multiplexer_1_out), .count(or_5_out), .Q(Data_out), .clk(Clk), .clr(Reset));  // open: carry
  Counter #(.width(24), .max('hffffff)) Stack_Pointer (
    .load(or_3_out), .D(bit_extender_1_out), .count(or_4_out), .Q(Stack_Pointer_q), .clk(or_1_out),
    .clr(Reset));  // open: carry
  RAM #(.addrWidth(24), .dataWidth(32), .bus("separate")) ram_1 (
    .addr(Stack_Pointer_q), .din(Data_out), .data(ram_1_data), .str(Push), .sel(Power), .clk(Clk),
    .ld(not_1_out), .clr(Reset));
  not not_1 (not_1_out, Push);
  Pull_Resistor pull_resistor_13 (.node(Data_out));
endmodule

module Loading_proqrams_device (
  input  [31:0] Data_in,
  input  Clk,
  input  Reset_Stop_loading,
  input  Power,
  input  Load__Access_to_Load,
  input  [23:0] \Сдвиг_Адреса_загрузки__Диск ,
  output [31:0] _1,
  output [31:0] _2,
  output [31:0] _3,
  output [31:0] _4,
  output Loading_Complete,
  output Load_RAM,
  output [23:0] Adress_for_loading_to_Comand_Protocol,
  output Loading,
  output [23:0] Adress_for_loading__for_Disk
);

  wire and_2_out, and_3_out, and_4_out, and_5_out, and_6_out, and_7_out, comparator_1_eq, comparator_2_eq,
       comparator_3_eq, comparator_4_eq, comparator_5_eq, comparator_6_eq, comparator_7_eq, comparator_8_eq,
       counter_2_carry, or_1_out, or_2_out, pull_resistor_4_node;
  wire [1:0] counter_1_q;
  wire [23:0] register_2_q;

  Pull_Resistor pull_resistor_1 (.node(Power));
  Pull_Resistor pull_resistor_2 (.node(Data_in));
  Pull_Resistor pull_resistor_3 (.node(Clk));
  Pull_Resistor pull_resistor_4 (.node(pull_resistor_4_node));
  Pull_Resistor pull_resistor_5 (.node(Reset_Stop_loading));
  Pull_Resistor pull_resistor_6 (.node(\Сдвиг_Адреса_загрузки__Диск ));
  and and_1 (pull_resistor_4_node, Load__Access_to_Load, ~Loading);  // AND_Gate
  or or_1 (or_1_out, and_7_out, Reset_Stop_loading, ~Power, counter_2_carry);  // OR_Gate
  Counter #(.width(2), .max('h3)) counter_1 (
    .load(1'b0), .D(2'b00), .count(Loading), .Q(counter_1_q), .carry(Load_RAM), .clk(Clk), .clr(or_1_out));
  Register #(.width(1)) register_1 (
    .D(pull_resistor_4_node), .en(pull_resistor_4_node), .Q(Loading), .clk(pull_resistor_4_node),
    .clr(or_1_out));
  Counter #(.width(24), .max('hffffff)) counter_2 (
    .load(1'b0), .D({24{1'b0}}), .count(Loading), .Q(Adress_for_loading_to_Comand_Protocol),
    .carry(counter_2_carry), .clk(Load_RAM), .clr(or_1_out));
  Register #(.width(24)) register_2 (
    .D(\Сдвиг_Адреса_загрузки__Диск ), .en(pull_resistor_4_node), .Q(register_2_q),
    .clk(pull_resistor_4_node), .clr(or_1_out));
  or or_2 (or_2_out, pull_resistor_4_node, comparator_1_eq);
  Comparator #(.width(2)) comparator_1 (.a(counter_1_q), .b(2'b00), .eq(comparator_1_eq));  // open: gt, lt
  Comparator #(.width(2)) comparator_2 (.a(counter_1_q), .b(2'b01), .eq(comparator_2_eq));  // open: gt, lt
  and and_2 (and_2_out, comparator_2_eq, Loading);
  Comparator #(.width(2)) comparator_3 (.a(counter_1_q), .b(2'b10), .eq(comparator_3_eq));  // open: gt, lt
  and and_3 (and_3_out, comparator_3_eq, Loading);
  Comparator #(.width(2)) comparator_4 (.a(counter_1_q), .b(2'b11), .eq(comparator_4_eq));  // open: gt, lt
  and and_4 (and_4_out, comparator_4_eq, Loading);
  Adder #(.width(24)) adder_1 (
    .a(Adress_for_loading_to_Comand_Protocol), .b(register_2_q), .out(Adress_for_loading__for_Disk));  // open: cin, cout
  Register #(.width(32)) register_3 (.D(Data_in), .en(and_5_out), .Q(_1), .clk(Clk), .clr(or_1_out));
  and and_5 (and_5_out, or_2_out, Loading);
  Register #(.width(32)) register_4 (.D(Data_in), .en(and_2_out), .Q(_2), .clk(Clk), .clr(or_1_out));
  Register #(.width(32)) register_5 (.D(Data_in), .en(and_3_out), .Q(_3), .clk(Clk), .clr(or_1_out));
  Register #(.width(32)) register_6 (.D(Data_in), .en(and_4_out), .Q(_4), .clk(Clk), .clr(or_1_out));
  or or_3 (Loading_Complete, counter_2_carry, and_7_out);
  Comparator #(.width(32)) comparator_5 (.a(_1), .b({32{1'b0}}), .eq(comparator_5_eq));  // open: gt, lt
  Comparator #(.width(32)) comparator_6 (.a(_2), .b({32{1'b0}}), .eq(comparator_6_eq));  // open: gt, lt
  Comparator #(.width(32)) comparator_7 (.a(_3), .b({32{1'b0}}), .eq(comparator_7_eq));  // open: gt, lt
  Comparator #(.width(32)) comparator_8 (.a(_4), .b({32{1'b0}}), .eq(comparator_8_eq));  // open: gt, lt
  Pull_Resistor pull_resistor_7 (.node(Adress_for_loading_to_Comand_Protocol));
  Pull_Resistor pull_resistor_8 (.node(Loading_Complete));
  Pull_Resistor pull_resistor_9 (.node(Loading));
  Pull_Resistor pull_resistor_10 (.node(Adress_for_loading__for_Disk));
  and and_6 (and_6_out, comparator_5_eq, comparator_6_eq, comparator_7_eq, comparator_8_eq);
  Pull_Resistor pull_resistor_11 (.node(_3));
  Pull_Resistor pull_resistor_12 (.node(Load_RAM));
  Pull_Resistor pull_resistor_13 (.node(_1));
  Pull_Resistor pull_resistor_14 (.node(_2));
  Pull_Resistor pull_resistor_15 (.node(_4));
  and and_7 (and_7_out, Load_RAM, Loading, and_6_out);
endmodule

module \строение_логических_элементов  (
  input  in_1,
  input  in_2,
  input  in_3,
  input  in_4,
  input  in_5,
  input  in_6,
  input  in_7,
  input  in_8,
  input  in_9,
  input  in_10,
  input  in_11,
  input  in_12,
  input  in_13,
  input  in_14,
  input  in_15,
  input  in_16,
  input  in_17,
  input  in_18,
  input  in_19,
  input  in_20,
  input  in_21,
  input  in_22,
  input  in_23,
  input  in_24,
  input  in_25,
  input  in_26,
  input  in_27,
  input  in_28,
  input  in_29,
  input  in_30,
  input  in_31,
  input  in_32,
  input  in_33,
  input  in_34,
  input  in_35,
  input  in_36,
  input  in_37,
  input  in_38,
  input  in_39,
  input  in_40,
  input  in_41,
  input  in_42,
  input  in_43,
  input  in_44,
  output out_45,
  output out_46,
  output out_47,
  output out_48,
  output out_49,
  output out_50,
  output out_51,
  output out_52,
  output out_53,
  output out_54,
  output out_55,
  output out_56,
  output out_57,
  output out_58,
  output out_59,
  output out_60,
  output out_61,
  output out_62,
  output out_63,
  output out_64,
  output out_65,
  output out_66,
  output out_67,
  output out_68,
  output out_69,
  output out_70
);

  wire and_2_out, and_4_out, nand_1_out, or_2_out, pull_resistor_2_node, transistor_5_out, transistor_8_out,
       transistor_10_out, transistor_12_out, xor_2_out;

  not not_1 (out_45, in_1);
  buf buffer_1 (out_47, in_3);
  and and_1 (out_49, in_5, in_7);
  or or_1 (out_51, in_9, in_11);
  xor xor_1 (out_53, in_13, in_15);
  assign out_55 = in_19 ? in_17 : 1'bz;  // Controlled_Buffer controlled_buffer_1
  Multiplexer multiplexer_1 (.in0(in_21), .in1(in_23), .out(out_57), .sel(in_25), .en(in_27));
  Demultiplexer demultiplexer_1 (.out0(out_59), .out1(out_61), .in(in_29), .sel(in_33), .en(in_31));
  Decoder decoder_1 (.out0(out_63), .out1(out_65), .sel(in_37), .en(in_35));
  Adder #(.width(1)) adder_1 (.a(in_41), .b(in_43), .out(out_68), .cin(in_39), .cout(out_69));
  Transistor transistor_1 (.in(1'b1), .out(out_46), .gate(in_2));
  Transistor #(.\type ("n"), .gate("br")) transistor_2 (.in(1'b0), .out(out_46), .gate(in_2));
  Transistor transistor_3 (.in(1'b0), .out(out_48), .gate(in_4));
  Transistor #(.\type ("n"), .gate("br")) transistor_4 (.in(1'b1), .out(out_48), .gate(in_4));
  Transistor #(.\type ("n")) transistor_5 (.in(1'b1), .out(transistor_5_out), .gate(in_6));
  Transistor transistor_6 (.in(1'b0), .out(out_50), .gate(in_8));
  Transistor #(.gate("br")) transistor_7 (.in(1'b0), .out(out_50), .gate(in_6));
  Transistor transistor_8 (.in(1'b0), .out(transistor_8_out), .gate(in_12));
  or or_2 (or_2_out, in_14, in_16);
  nand nand_1 (nand_1_out, in_16, in_14);
  Transistor #(.\type ("n"), .gate("br")) transistor_9 (.in(in_18), .out(out_56), .gate(in_20));
  Transistor transistor_10 (.in(in_22), .out(transistor_10_out), .gate(in_26));
  Transistor #(.\type ("n"), .gate("br")) transistor_11 (.in(in_24), .out(transistor_10_out), .gate(in_26));
  Transistor transistor_12 (.in(in_30), .out(transistor_12_out), .gate(in_34));
  Pull_Resistor pull_resistor_1 (.node(transistor_12_out));
  Pull_Resistor pull_resistor_2 (.node(pull_resistor_2_node));
  Transistor #(.\type ("n"), .gate("br")) transistor_13 (.in(in_30), .out(pull_resistor_2_node), .gate(in_34));
  Demultiplexer demultiplexer_2 (.out0(out_64), .out1(out_66), .in(1'b1), .sel(in_38), .en(in_36));
  xor xor_2 (xor_2_out, in_42, in_44);
  and and_2 (and_2_out, in_42, in_44);
  Transistor #(.\type ("n")) transistor_14 (.in(transistor_5_out), .out(out_50), .gate(in_8));
  Transistor #(.\type ("n")) transistor_15 (.in(1'b1), .out(out_52), .gate(in_10));
  Transistor #(.\type ("n"), .gate("br")) transistor_16 (.in(1'b1), .out(out_52), .gate(in_12));
  Transistor transistor_17 (.in(transistor_8_out), .out(out_52), .gate(in_10));
  and and_3 (out_54, or_2_out, nand_1_out);
  Transistor #(.\type ("n"), .gate("br")) transistor_18 (.in(transistor_10_out), .out(out_58), .gate(in_28));
  Transistor #(.\type ("n")) transistor_19 (.in(transistor_12_out), .out(out_60), .gate(in_32));
  Transistor #(.\type ("n"), .gate("br")) transistor_20 (.in(pull_resistor_2_node), .out(out_62), .gate(in_32));
  xor xor_3 (out_67, in_40, xor_2_out);
  and and_4 (and_4_out, in_40, xor_2_out);
  or or_3 (out_70, and_4_out, and_2_out);
endmodule

module Shared_Registers (
  input  [31:0] Data_in,
  input  Power,
  input  [4:0] Choose_Register,
  input  Load,
  input  Reset_choosed_register,
  input  Reset_all,
  input  Clk,
  input  [4:0] \С1 ,
  input  [4:0] \С2 ,
  input  [4:0] \С3 ,
  output [31:0] Data_out__1,
  output [31:0] Data_out__2,
  output [31:0] Data_out__3
);

  wire and_1_out, and_2_out, and_3_out, and_4_out, and_5_out, and_6_out, and_7_out, and_8_out, and_9_out,
       and_10_out, and_11_out, and_12_out, and_13_out, and_14_out, and_15_out, and_16_out, and_17_out,
       and_18_out, and_19_out, and_20_out, and_21_out, and_22_out, and_23_out, and_24_out, and_25_out,
       and_26_out, and_27_out, and_28_out, and_29_out, and_30_out, and_31_out, and_32_out, and_33_out,
       and_34_out, and_35_out, and_36_out, and_37_out, and_38_out, and_39_out, and_40_out, and_41_out,
       and_42_out, and_43_out, and_44_out, and_45_out, and_46_out, and_47_out, and_48_out, and_49_out,
       and_50_out, and_51_out, and_52_out, and_53_out, and_54_out, and_55_out, and_56_out, and_57_out,
       and_58_out, and_59_out, and_60_out, and_61_out, and_62_out, and_63_out, and_64_out, decoder_1_out0,
       decoder_1_out1, decoder_1_out2, decoder_1_out3, decoder_1_out4, decoder_1_out5, decoder_1_out6,
       decoder_1_out7, decoder_1_out8, decoder_1_out9, decoder_1_out10, decoder_1_out11, decoder_1_out12,
       decoder_1_out13, decoder_1_out14, decoder_1_out15, decoder_1_out16, decoder_1_out17, decoder_1_out18,
       decoder_1_out19, decoder_1_out20, decoder_1_out21, decoder_1_out22, decoder_1_out23, decoder_1_out24,
       decoder_1_out25, decoder_1_out26, decoder_1_out27, decoder_1_out28, decoder_1_out29, decoder_1_out30,
       decoder_1_out31, or_1_out, or_2_out, or_3_out, or_4_out, or_5_out, or_6_out, or_7_out, or_8_out,
       or_9_out, or_10_out, or_11_out, or_12_out, or_13_out, or_14_out, or_15_out, or_16_out, or_17_out,
       or_18_out, or_19_out, or_20_out, or_21_out, or_22_out, or_23_out, or_24_out, or_25_out, or_26_out,
       or_27_out, or_28_out, or_29_out, or_30_out, or_31_out, or_32_out;
  wire [31:0] register_1_q, register_2_q, register_3_q, register_4_q, register_5_q, register_6_q,
       register_7_q, register_8_q, register_9_q, register_10_q, register_11_q, register_12_q, register_13_q,
       register_14_q, register_15_q, register_16_q, register_17_q, register_18_q, register_19_q,
       register_20_q, register_21_q, register_22_q, register_23_q, register_24_q, register_25_q,
       register_26_q, register_27_q, register_28_q, register_29_q, register_30_q, register_31_q,
       register_32_q, undriven;

  Pull_Resistor pull_resistor_1 (.node(Choose_Register));
  Pull_Resistor pull_resistor_2 (.node(Data_in));
  Pull_Resistor pull_resistor_3 (.node(Power));
  Pull_Resistor pull_resistor_4 (.node(Clk));
  Pull_Resistor pull_resistor_5 (.node(Load));
  Pull_Resistor pull_resistor_6 (.node(\С1 ));
  Pull_Resistor pull_resistor_7 (.node(\С2 ));
  Pull_Resistor pull_resistor_8 (.node(Reset_choosed_register));
  Pull_Resistor pull_resistor_9 (.node(\С3 ));
  Pull_Resistor pull_resistor_10 (.node(Reset_all));
  Decoder #(.select(5), .disabled(0)) decoder_1 (
    .out0(decoder_1_out0), .out1(decoder_1_out1), .out2(decoder_1_out2), .out3(decoder_1_out3),
    .out4(decoder_1_out4), .out5(decoder_1_out5), .out6(decoder_1_out6), .out7(decoder_1_out7),
    .out8(decoder_1_out8), .out9(decoder_1_out9), .out10(decoder_1_out10), .out11(decoder_1_out11),
    .out12(decoder_1_out12), .out13(decoder_1_out13), .out14(decoder_1_out14), .out15(decoder_1_out15),
    .out16(decoder_1_out16), .out17(decoder_1_out17), .out18(decoder_1_out18), .out19(decoder_1_out19),
    .out20(decoder_1_out20), .out21(decoder_1_out21), .out22(decoder_1_out22), .out23(decoder_1_out23),
    .out24(decoder_1_out24), .out25(decoder_1_out25), .out26(decoder_1_out26), .out27(decoder_1_out27),
    .out28(decoder_1_out28), .out29(decoder_1_out29), .out30(decoder_1_out30), .out31(decoder_1_out31),
    .sel(Choose_Register), .en(Power));
  and and_1 (and_1_out, Load, decoder_1_out0);
  and and_2 (and_2_out, decoder_1_out0, Reset_choosed_register);
  or or_1 (or_1_out, and_2_out, Reset_all);
  and and_3 (and_3_out, Load, decoder_1_out1);
  and and_4 (and_4_out, decoder_1_out1, Reset_choosed_register);
  or or_2 (or_2_out, and_4_out, Reset_all);
  and and_5 (and_5_out, Load, decoder_1_out2);
  and and_6 (and_6_out, decoder_1_out2, Reset_choosed_register);
  or or_3 (or_3_out, and_6_out, Reset_all);
  and and_7 (and_7_out, Load, decoder_1_out3);
  and and_8 (and_8_out, decoder_1_out3, Reset_choosed_register);
  or or_4 (or_4_out, and_8_out, Reset_all);
  and and_9 (and_9_out, Load, decoder_1_out4);
  and and_10 (and_10_out, decoder_1_out4, Reset_choosed_register);
  or or_5 (or_5_out, and_10_out, Reset_all);
  and and_11 (and_11_out, Load, decoder_1_out5);
  and and_12 (and_12_out, decoder_1_out5, Reset_choosed_register);
  or or_6 (or_6_out, and_12_out, Reset_all);
  and and_13 (and_13_out, Load, decoder_1_out6);
  and and_14 (and_14_out, decoder_1_out6, Reset_choosed_register);
  or or_7 (or_7_out, and_14_out, Reset_all);
  and and_15 (and_15_out, Load, decoder_1_out7);
  and and_16 (and_16_out, decoder_1_out7, Reset_choosed_register);
  or or_8 (or_8_out, and_16_out, Reset_all);
  and and_17 (and_17_out, Load, decoder_1_out8);
  and and_18 (and_18_out, decoder_1_out8, Reset_choosed_register);
  or or_9 (or_9_out, and_18_out, Reset_all);
  and and_19 (and_19_out, Load, decoder_1_out9);
  and and_20 (and_20_out, decoder_1_out9, Reset_choosed_register);
  or or_10 (or_10_out, and_20_out, Reset_all);
  and and_21 (and_21_out, Load, decoder_1_out10);
  and and_22 (and_22_out, decoder_1_out10, Reset_choosed_register);
  or or_11 (or_11_out, and_22_out, Reset_all);
  and and_23 (and_23_out, Load, decoder_1_out11);
  and and_24 (and_24_out, decoder_1_out11, Reset_choosed_register);
  or or_12 (or_12_out, and_24_out, Reset_all);
  and and_25 (and_25_out, Load, decoder_1_out12);
  and and_26 (and_26_out, decoder_1_out12, Reset_choosed_register);
  or or_13 (or_13_out, and_26_out, Reset_all);
  and and_27 (and_27_out, Load, decoder_1_out13);
  and and_28 (and_28_out, decoder_1_out13, Reset_choosed_register);
  or or_14 (or_14_out, and_28_out, Reset_all);
  and and_29 (and_29_out, Load, decoder_1_out14);
  and and_30 (and_30_out, decoder_1_out14, Reset_choosed_register);
  or or_15 (or_15_out, and_30_out, Reset_all);
  and and_31 (and_31_out, Load, decoder_1_out15);
  and and_32 (and_32_out, decoder_1_out15, Reset_choosed_register);
  or or_16 (or_16_out, and_32_out, Reset_all);
  and and_33 (and_33_out, Load, decoder_1_out16);
  and and_34 (and_34_out, decoder_1_out16, Reset_choosed_register);
  or or_17 (or_17_out, and_34_out, Reset_all);
  and and_35 (and_35_out, Load, decoder_1_out17);
  and and_36 (and_36_out, decoder_1_out17, Reset_choosed_register);
  or or_18 (or_18_out, and_36_out, Reset_all);
  and and_37 (and_37_out, Load, decoder_1_out18);
  and and_38 (and_38_out, decoder_1_out18, Reset_choosed_register);
  or or_19 (or_19_out, and_38_out, Reset_all);
  and and_39 (and_39_out, Load, decoder_1_out19);
  and and_40 (and_40_out, decoder_1_out19, Reset_choosed_register);
  or or_20 (or_20_out, and_40_out, Reset_all);
  and and_41 (and_41_out, Load, decoder_1_out20);
  and and_42 (and_42_out, decoder_1_out20, Reset_choosed_register);
  or or_21 (or_21_out, and_42_out, Reset_all);
  and and_43 (and_43_out, Load, decoder_1_out21);
  and and_44 (and_44_out, decoder_1_out21, Reset_choosed_register);
  or or_22 (or_22_out, and_44_out, Reset_all);
  and and_45 (and_45_out, Load, decoder_1_out22);
  and and_46 (and_46_out, decoder_1_out22, Reset_choosed_register);
  or or_23 (or_23_out, and_46_out, Reset_all);
  and and_47 (and_47_out, Load, decoder_1_out23);
  and and_48 (and_48_out, decoder_1_out23, Reset_choosed_register);
  or or_24 (or_24_out, and_48_out, Reset_all);
  and and_49 (and_49_out, Load, decoder_1_out24);
  and and_50 (and_50_out, decoder_1_out24, Reset_choosed_register);
  or or_25 (or_25_out, and_50_out, Reset_all);
  and and_51 (and_51_out, Load, decoder_1_out25);
  and and_52 (and_52_out, decoder_1_out25, Reset_choosed_register);
  or or_26 (or_26_out, and_52_out, Reset_all);
  and and_53 (and_53_out, Load, decoder_1_out26);
  and and_54 (and_54_out, decoder_1_out26, Reset_choosed_register);
  or or_27 (or_27_out, and_54_out, Reset_all);
  and and_55 (and_55_out, Load, decoder_1_out27);
  and and_56 (and_56_out, decoder_1_out27, Reset_choosed_register);
  or or_28 (or_28_out, and_56_out, Reset_all);
  and and_57 (and_57_out, Load, decoder_1_out28);
  and and_58 (and_58_out, decoder_1_out28, Reset_choosed_register);
  or or_29 (or_29_out, and_58_out, Reset_all);
  and and_59 (and_59_out, Load, decoder_1_out29);
  and and_60 (and_60_out, decoder_1_out29, Reset_choosed_register);
  or or_30 (or_30_out, and_60_out, Reset_all);
  and and_61 (and_61_out, Load, decoder_1_out30);
  and and_62 (and_62_out, decoder_1_out30, Reset_choosed_register);
  or or_31 (or_31_out, and_62_out, Reset_all);
  and and_63 (and_63_out, Load, decoder_1_out31);
  and and_64 (and_64_out, decoder_1_out31, Reset_choosed_register);
  or or_32 (or_32_out, and_64_out, Reset_all);
  Register #(.width(32)) register_1 (.D(Data_in), .en(and_1_out), .Q(register_1_q), .clk(Clk), .clr(or_1_out));
  Register #(.width(32)) register_2 (.D(Data_in), .en(and_3_out), .Q(register_2_q), .clk(Clk), .clr(or_2_out));
  Register #(.width(32)) register_3 (.D(Data_in), .en(and_5_out), .Q(register_3_q), .clk(Clk), .clr(or_3_out));
  Register #(.width(32)) register_4 (.D(Data_in), .en(and_7_out), .Q(register_4_q), .clk(Clk), .clr(or_4_out));
  Register #(.width(32)) register_5 (.D(Data_in), .en(and_9_out), .Q(register_5_q), .clk(Clk), .clr(or_5_out));
  Register #(.width(32)) register_6 (.D(Data_in), .en(and_11_out), .Q(register_6_q), .clk(Clk), .clr(or_6_out));
  Register #(.width(32)) register_7 (.D(Data_in), .en(and_13_out), .Q(register_7_q), .clk(Clk), .clr(or_7_out));
  Register #(.width(32)) register_8 (.D(Data_in), .en(and_15_out), .Q(register_8_q), .clk(Clk), .clr(or_8_out));
  Register #(.width(32)) register_9 (.D(undriven), .en(and_17_out), .Q(register_9_q), .clk(Clk), .clr(or_9_out));
  Register #(.width(32)) register_10 (.D(undriven), .en(and_19_out), .Q(register_10_q), .clk(Clk), .clr(or_10_out));
  Register #(.width(32)) register_11 (.D(undriven), .en(and_21_out), .Q(register_11_q), .clk(Clk), .clr(or_11_out));
  Register #(.width(32)) register_12 (.D(undriven), .en(and_23_out), .Q(register_12_q), .clk(Clk), .clr(or_12_out));
  Register #(.width(32)) register_13 (.D(undriven), .en(and_25_out), .Q(register_13_q), .clk(Clk), .clr(or_13_out));
  Register #(.width(32)) register_14 (.D(undriven), .en(and_27_out), .Q(register_14_q), .clk(Clk), .clr(or_14_out));
  Register #(.width(32)) register_15 (.D(undriven), .en(and_29_out), .Q(register_15_q), .clk(Clk), .clr(or_15_out));
  Register #(.width(32)) register_16 (.D(undriven), .en(and_31_out), .Q(register_16_q), .clk(Clk), .clr(or_16_out));
  Register #(.width(32)) register_17 (.D(Data_in), .en(and_33_out), .Q(register_17_q), .clk(Clk), .clr(or_17_out));
  Register #(.width(32)) register_18 (.D(Data_in), .en(and_35_out), .Q(register_18_q), .clk(Clk), .clr(or_18_out));
  Register #(.width(32)) register_19 (.D(Data_in), .en(and_37_out), .Q(register_19_q), .clk(Clk), .clr(or_19_out));
  Register #(.width(32)) register_20 (.D(Data_in), .en(and_39_out), .Q(register_20_q), .clk(Clk), .clr(or_20_out));
  Register #(.width(32)) register_21 (.D(Data_in), .en(and_41_out), .Q(register_21_q), .clk(Clk), .clr(or_21_out));
  Register #(.width(32)) register_22 (.D(Data_in), .en(and_43_out), .Q(register_22_q), .clk(Clk), .clr(or_22_out));
  Register #(.width(32)) register_23 (.D(Data_in), .en(and_45_out), .Q(register_23_q), .clk(Clk), .clr(or_23_out));
  Register #(.width(32)) register_24 (.D(Data_in), .en(and_47_out), .Q(register_24_q), .clk(Clk), .clr(or_24_out));
  Register #(.width(32)) register_25 (.D(Data_in), .en(and_49_out), .Q(register_25_q), .clk(Clk), .clr(or_25_out));
  Register #(.width(32)) register_26 (.D(Data_in), .en(and_51_out), .Q(register_26_q), .clk(Clk), .clr(or_26_out));
  Register #(.width(32)) register_27 (.D(Data_in), .en(and_53_out), .Q(register_27_q), .clk(Clk), .clr(or_27_out));
  Register #(.width(32)) register_28 (.D(Data_in), .en(and_55_out), .Q(register_28_q), .clk(Clk), .clr(or_28_out));
  Register #(.width(32)) register_29 (.D(Data_in), .en(and_57_out), .Q(register_29_q), .clk(Clk), .clr(or_29_out));
  Register #(.width(32)) register_30 (.D(Data_in), .en(and_59_out), .Q(register_30_q), .clk(Clk), .clr(or_30_out));
  Register #(.width(32)) register_31 (.D(Data_in), .en(and_61_out), .Q(register_31_q), .clk(Clk), .clr(or_31_out));
  Register #(.width(32)) register_32 (.D(Data_in), .en(and_63_out), .Q(register_32_q), .clk(Clk), .clr(or_32_out));
  Multiplexer #(.select(5), .width(32), .disabled(0), .enable("false")) multiplexer_1 (
    .in0(register_1_q), .in1(register_2_q), .in2(register_3_q), .in3(register_4_q), .in4(register_5_q),
    .in5(register_6_q), .in6(register_7_q), .in7(register_8_q), .in8(register_9_q), .in9(register_10_q),
    .in10(register_11_q), .in11(register_12_q), .in12(register_13_q), .in13(register_14_q),
    .in14(register_15_q), .in15(register_16_q), .in16(register_17_q), .in17(register_18_q),
    .in18(register_19_q), .in19(register_20_q), .in20(register_21_q), .in21(register_22_q),
    .in22(register_23_q), .in23(register_24_q), .in24(register_25_q), .in25(register_26_q),
    .in26(register_27_q), .in27(register_28_q), .in28(register_29_q), .in29(register_30_q),
    .in30(register_31_q), .in31(register_32_q), .out(Data_out__1), .sel(\С1 ));
  Pull_Resistor pull_resistor_11 (.node(Data_out__1));
  Multiplexer #(.select(5), .width(32), .disabled(0), .enable("false")) multiplexer_2 (
    .in0(register_1_q), .in1(register_2_q), .in2(register_3_q), .in3(register_4_q), .in4(register_5_q),
    .in5(register_6_q), .in6(register_7_q), .in7(register_8_q), .in8(register_9_q), .in9(register_10_q),
    .in10(register_11_q), .in11(register_12_q), .in12(register_13_q), .in13(register_14_q),
    .in14(register_15_q), .in15(register_16_q), .in16(register_17_q), .in17(register_18_q),
    .in18(register_19_q), .in19(register_20_q), .in20(register_21_q), .in21(register_22_q),
    .in22(register_23_q), .in23(register_24_q), .in24(register_25_q), .in25(register_26_q),
    .in26(register_27_q), .in27(register_28_q), .in28(register_29_q), .in29(register_30_q),
    .in30(register_31_q), .in31(register_32_q), .out(Data_out__2), .sel(\С2 ));
  Pull_Resistor pull_resistor_12 (.node(Data_out__2));
  Multiplexer #(.select(5), .width(32), .disabled(0), .enable("false")) multiplexer_3 (
    .in0(register_1_q), .in1(register_2_q), .in2(register_3_q), .in3(register_4_q), .in4(register_5_q),
    .in5(register_6_q), .in6(register_7_q), .in7(register_8_q), .in8(register_9_q), .in9(register_10_q),
    .in10(register_11_q), .in11(register_12_q), .in12(register_13_q), .in13(register_14_q),
    .in14(register_15_q), .in15(register_16_q), .in16(register_17_q), .in17(register_18_q),
    .in18(register_19_q), .in19(register_20_q), .in20(register_21_q), .in21(register_22_q),
    .in22(register_23_q), .in23(register_24_q), .in24(register_25_q), .in25(register_26_q),
    .in26(register_27_q), .in27(register_28_q), .in28(register_29_q), .in29(register_30_q),
    .in30(register_31_q), .in31(register_32_q), .out(Data_out__3), .sel(\С3 ));
  Pull_Resistor pull_resistor_13 (.node(Data_out__3));
endmodule

module DDR_Shader_Register (
  input  [4:0] Adress_1,
  input  [4:0] Adress_2,
  input  Power,
  input  Reset,
  input  Clk,
  input  WE_1,
  input  WE_2,
  input  [31:0] Data_in_1,
  input  [31:0] Data_in_2,
  output [31:0] Data_out
);

  wire and_1_out, and_2_out, nor_1_out, or_1_out;
  wire [4:0] multiplexer_1_out;
  wire [31:0] controlled_buffer_1_out, ram_1_data;

  and and_1 (and_1_out, Clk, WE_1);
  and and_2 (and_2_out, ~Clk, WE_2);  // AND_Gate
  assign controlled_buffer_1_out = and_1_out ? Data_in_1 : 32'bz;  // Controlled_Buffer controlled_buffer_1
  assign controlled_buffer_1_out = and_2_out ? Data_in_2 : 32'bz;  // Controlled_Buffer controlled_buffer_2
  Multiplexer #(.width(5)) multiplexer_1 (
    .in0(Adress_1), .in1(Adress_2), .out(multiplexer_1_out), .sel(Clk), .en(Power));
  or or_1 (or_1_out, and_1_out, and_2_out);
  nor nor_1 (nor_1_out, and_1_out, and_2_out);
  Register #(.width(32)) register_1 (.D(ram_1_data), .en(Power), .Q(Data_out), .clk(Clk), .clr(Reset));
  RAM #(.addrWidth(5), .dataWidth(32), .bus("separate")) ram_1 (
    .addr(multiplexer_1_out), .din(controlled_buffer_1_out), .data(ram_1_data), .str(or_1_out), .sel(Power),
    .clk(or_1_out), .ld(nor_1_out), .clr(Reset));
  Pull_Resistor pull_resistor_1 (.node(Data_out));
endmodule
